# Fritzing sketch game (saved by Fritzing 0.9.3b)
circuit board: 19.3284cm x 15.4269cm
breadboards: 1

parts:
  U1 = ESP32-38PinWide [part_number=ESP32-38PinWide]
  hc-sr1 = hc-sr04
  U2 = TA7291P [package=HSIP10-P-2.54(THT)]
  VCC1 = Battery
  M1 = DC Motor
  S1 = SWITCH-MOMENTARY-2 [package=tactile-pth-12mm]
  J1 = Piezo Speaker

nets:
  N1: U1.GPIO32, hc-sr1.Trig
  N2: U1.GPIO33, hc-sr1.Echo
  GND: U1.GND, hc-sr1.GND, S1.1, J1.pin2
  N3: U1.GPIO13, J1.pin1
  VCC: U1.VIN, hc-sr1.VCC, U2.Vcc
  N4: U1.GPIO2, U2.IN2
  N5: U1.GPIO0, U2.IN1
  N6: U1.GPIO4, U2.Vref
  N7: U1.GPIO18, S1.2
  N8: U2.GND, VCC1.-
  N9: U2.OUT1, M1.pin_1
  N10: U2.Vs, VCC1.+
  N11: U2.OUT2, M1.pin_2

custom parts:
  ESP32-38PinWide: Generic 38-Pin ESP32 with wide format (only access to one side of pins on a breadboard) based on Stephen Lilley's HiLetgo ESP-WROOM-32 ESP32 ESP-32S Development Board.
  TA7291P: The IC are Full-Bridge Driver. 4 modes available (CW / CCW / STOP / BRAKE) and PWM control. Output current:1.0 A (AVE.) 2.0 A (PEAK)
